// Logisim project comb_logic.circ as structural Verilog: 1 circuit, main circuit main
module main (
  input  A,
  input  B,
  input  C,
  input  D,
  output X
);

  wire and_1_out, and_2_out, and_3_out, not_1_out, not_2_out, not_3_out, not_4_out, or_1_out, xor_1_out;

  not not_1 (not_1_out, A);
  not not_2 (not_2_out, B);
  xor xor_1 (xor_1_out, C, D);
  not not_3 (not_3_out, C);
  not not_4 (not_4_out, D);
  or or_1 (or_1_out, not_2_out, xor_1_out);
  and and_1 (and_1_out, A, not_2_out, C);
  and and_2 (and_2_out, not_1_out, or_1_out);
  and and_3 (and_3_out, B, not_3_out, not_4_out);
  or or_2 (X, and_1_out, and_2_out, and_3_out);
endmodule
